// Logisim project gcd.circ as structural Verilog: 1 circuit, main circuit main
module main (
  input  [31:0] x,
  input  in_2,
  input  [31:0] y,
  output [31:0] out_4
);

  wire button_1_out, clock_1_out, d_ff_1_q, main_1_ldo, main_1_ldx, main_1_ldy, main_1_ss, main_1_sx,
       main_1_sy, main_2_eq, main_2_gt, main_2_lt;

  Clock clock_1 (.out(clock_1_out));
  gcd_controller_main main_1 (
    .clk(clock_1_out), .goi(in_2), .eq(main_2_eq), .gt(main_2_gt), .lt(main_2_lt), .ldo(main_1_ldo),
    .ldx(main_1_ldx), .ldy(main_1_ldy), .sx(main_1_sx), .sy(main_1_sy), .ss(main_1_ss));
  gcd_datapath_main main_2 (
    .x(x), .clk(clock_1_out), .ldx(main_1_ldx), .ldy(main_1_ldy), .ldo(main_1_ldo), .y(y), .ss(main_1_ss),
    .sx(main_1_sx), .sy(main_1_sy), .gt(main_2_gt), .eq(main_2_eq), .lt(main_2_lt), .obeb(out_4));
  Button button_1 (.out(button_1_out));
  LED led_1 (.in(d_ff_1_q));
  D_Flip_Flop d_ff_1 (.clk(main_2_eq), .D(1'b1), .Q(d_ff_1_q), .reset(button_1_out));  // open: Qn, preset, en
endmodule
