// Logisim project gcd_controller.circ as structural Verilog: 1 circuit, main circuit main
module main (
  input  clk,
  input  goi,
  input  eq,
  input  gt,
  input  lt,
  output ldo,
  output ldx,
  output ldy,
  output sx,
  output sy,
  output ss
);

  wire and_2_out, and_3_out, decoder_1_out0, not_1_out, not_2_out, or_1_out;
  wire [1:0] or_4_out, State_q;

  Register #(.width(2)) State (.D(or_4_out), .Q(State_q), .clk(clk));  // open: en, clr
  not not_1 (not_1_out, State_q[1]);
  Decoder #(.select(2), .enable("false")) decoder_1 (
    .out0(decoder_1_out0), .out1(ldo), .out2(sx), .out3(ss), .sel(State_q));
  or or_1 (or_1_out, gt, lt);
  and and_1 (or_4_out[1], State_q[0], not_1_out, or_1_out);
  not not_2 (not_2_out, State_q[0]);
  or or_2 (ldx, decoder_1_out0, sx);
  or or_3 (ldy, decoder_1_out0, ss);
  and and_2 (and_2_out, State_q[0], not_1_out, lt);
  and and_3 (and_3_out, not_2_out, goi);
  or or_4 (or_4_out[0], State_q[1], and_2_out, and_3_out);

  assign sy = ss;
endmodule
