// Logisim project gcd_datapath.circ as structural Verilog: 1 circuit, main circuit main
module main (
  input  [31:0] x,
  input  clk,
  input  ldx,
  input  ldy,
  input  ldo,
  input  [31:0] y,
  input  ss,
  input  sx,
  input  sy,
  output gt,
  output eq,
  output lt,
  output [31:0] obeb
);

  wire [31:0] multiplexer_1_out, multiplexer_2_out, multiplexer_3_out, multiplexer_4_out, subtractor_1_out,
       xi_q, yi_q;

  Multiplexer #(.width(32), .enable("false")) multiplexer_1 (
    .in0(x), .in1(subtractor_1_out), .out(multiplexer_1_out), .sel(sx));
  Multiplexer #(.width(32), .enable("false")) multiplexer_2 (
    .in0(y), .in1(subtractor_1_out), .out(multiplexer_2_out), .sel(sy));
  Register #(.width(32)) xi (.D(multiplexer_1_out), .en(ldx), .Q(xi_q), .clk(clk));  // open: clr
  Register #(.width(32)) yi (.D(multiplexer_2_out), .en(ldy), .Q(yi_q), .clk(clk));  // open: clr
  Multiplexer #(.width(32), .enable("false")) multiplexer_3 (.in0(xi_q), .in1(yi_q), .out(multiplexer_3_out), .sel(ss));
  Multiplexer #(.width(32), .enable("false")) multiplexer_4 (.in0(yi_q), .in1(xi_q), .out(multiplexer_4_out), .sel(ss));
  Comparator #(.width(32)) comparator_1 (.a(xi_q), .b(yi_q), .gt(gt), .eq(eq), .lt(lt));
  Subtractor #(.width(32)) subtractor_1 (
    .a(multiplexer_3_out), .b(multiplexer_4_out), .out(subtractor_1_out));  // open: bin, bout
  Register #(.width(32)) u_obeb (.D(xi_q), .en(ldo), .Q(obeb), .clk(clk));  // open: clr
endmodule
